# Fritzing sketch Otto2_wiring (saved by Fritzing 0.9.10b)

parts:
  Part1 = Arduino Nano (Rev3.0)
  M2_LeftLeg = Dagu DGServo 9g (Top view) [part_number=RS001B]
  M3_RightLeg = Dagu DGServo 9g (Top view) [part_number=RS001B]
  M4_LeftFoot = Dagu DGServo 9g (Top view) [part_number=RS001B]
  M5_RightFoot = Dagu DGServo 9g (Top view) [part_number=RS001B]
  Piezo_buzzer1 = Piezo Buzzer
  HC-SR04_Sensor_2 = HC-SR04 Ultrasonic Distance Sensor
  S1 = SWITCH-DPDT-latching [package=os]
  SparkFun_LiPo_Charger_Booster-5V1A1 = SparkFun LiPo Charger Booster-5V1A [part_number="PRT-14411 "]
  BATT1 = LiPoly Battery  # not connected
  TTP223B1 = TTP223B Capacitive Touch Sensor Module
  Mod1 = Nano-V3-0-IO-Expansion-Adapter

nets:
  N1: Part1.D1/TX, Mod1.D1/TX#65, Mod1.D0/RX#128
  N2: Part1.D0/RX, Mod1.D0/RX#64, Mod1.D1/TX#129
  N3: Part1.RESET, Mod1.RST
  GND: Part1.GND, M2_LeftLeg.gnd, M3_RightLeg.gnd, M4_LeftFoot.gnd, M5_RightFoot.gnd, Piezo_buzzer1.pin_1, HC-SR04_Sensor_2.GND, SparkFun_LiPo_Charger_Booster-5V1A1.GND, TTP223B1.GND, Mod1.GND
  N4: Part1.D2, M2_LeftLeg.pulse, Mod1.D2
  N5: Part1.D3, M3_RightLeg.pulse, Mod1.D3_PWM
  N6: Part1.D4, M4_LeftFoot.pulse, Mod1.D4
  N7: Part1.D5, M5_RightFoot.pulse, Mod1.D5_PWM
  N8: Part1.D6, Mod1.D6_PWM
  N9: Part1.D7, Mod1.D7
  N10: Part1.D8, HC-SR04_Sensor_2.TRIG, Mod1.D8
  N11: Part1.D9, HC-SR04_Sensor_2.ECHO, Mod1.D9_PWM
  N12: Part1.D10, Mod1.D10_PWM/SS
  N13: Part1.D11/MOSI, TTP223B1.SIG, Mod1.D11_PWM/MOSI
  N14: Part1.D12/MISO, Mod1.D12/MISO
  VIN: Part1.VIN, Mod1.VIN
  VCC: Part1.5V, M2_LeftLeg.vcc, M3_RightLeg.vcc, M4_LeftFoot.vcc, M5_RightFoot.vcc, HC-SR04_Sensor_2.VCC, SparkFun_LiPo_Charger_Booster-5V1A1.VCC, TTP223B1.VCC, Mod1.VCC
  N15: Part1.A7, Mod1.A7
  N16: Part1.A6, Mod1.A6
  N17: Part1.A5, Mod1.A5/SCL
  N18: Part1.A4, Mod1.A4/SDA
  N19: Part1.A3, Mod1.A3
  N20: Part1.A2, Mod1.A2
  N21: Part1.A1, Mod1.A1
  N22: Part1.A0, Mod1.A0
  N23: Part1.AREF, Mod1.AREF
  N24: Part1.3V3, Mod1.NC
  N25: Part1.D13/SCK, Piezo_buzzer1.pin_2, Mod1.D13/SCK
  N26: S1.1, SparkFun_LiPo_Charger_Booster-5V1A1.VBATT
  N27: S1.3, SparkFun_LiPo_Charger_Booster-5V1A1.1

notes:
  Leg Right: 3
  Foot Right: 5
  Leg Left: 2
  Foot Left: 4

custom parts:
  Piezo Buzzer: Piezo buzzer PS1420P02CT
  SWITCH-DPDT-latching: DPDT latching pushbutton switch
  SparkFun LiPo Charger Booster-5V1A: The SparkFun 5V/1A LiPo Charger/Booster is a no-nonsense circuit for generating one amp from a Lithium Polymer battery at 5V. This LiPo charger is a very economical choice that is equipped with a simple booster circuit utilizing the PAM2401 IC, and includes protection diodes so you can run multiple cells in series for an extra kick. While the booster circuit is in operation, this board can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
  LiPoly Battery: Lithium Ion Polymer Battery 3.7V 1200mAh
  TTP223B Capacitive Touch Sensor Module: The TTP223B capacitive touch sensor module uses the TTP223B IC. The appropriate voltage is approximately 2 to 5.5 volts.
  Nano-V3-0-IO-Expansion-Adapter: Nano V3.0 IO Expansion Adapter Shield. Note pcb view has been supressed as not useful. You can drag a Nano over the Nano connectors and it will connect and appear in schematic (although at present due to a bug, routing will not show as complete in breadboard).
